// Digital circuit RegisterFile_ALU.dig as structural Verilog
module RegisterFile_ALU (
  input  clk,
  input  Read_Register1,
  input  Read_Register2,
  input  Write_Register,
  input  ctrl,
  input  Opcode,
  input  Write_Data,
  input  Write_Select
);

  wire _8bitalu_1_p4, multiplexer_1_out, registerfile_1_p7, registerfile_1_p8;

  Multiplexer multiplexer_1 (.sel(Write_Select), .in_0(Write_Data), .in_1(_8bitalu_1_p4), .out(multiplexer_1_out));
  // RegisterFile registerfile_1: pin names not known; wires that end beside it: Read_Register1, Read_Register2, ctrl, multiplexer_1_out, Write_Register, clk, registerfile_1_p7, registerfile_1_p8
  // _8bitALU _8bitalu_1: pin names not known; wires that end beside it: registerfile_1_p7, registerfile_1_p8, Opcode, _8bitalu_1_p4
endmodule
